// Logisim project 12-bit-risc-v-microprocessor.circ as structural Verilog: 5 circuits, main circuit main
module main (
);

  register_file_12_bit register_file_12_bit_1 ();  // open: Write_Enabler, Write_Data, RD_Selector, DATA_1_RS, RS_Selector, DATA_2_RT, RT_Selector, CLOCK, Register_Clear
  ALU_12_bit alu_12_bit_1 ();  // open: A, B, Zero_Detector, Result, ALUOP, Cout___Bout___Upper_Bits_of_Product___Remainder
endmodule

module register_file_12_bit (
  input  Write_Enabler,
  input  [11:0] Write_Data,
  input  [2:0] RS_Selector,
  input  [2:0] RD_Selector,
  input  [2:0] RT_Selector,
  input  CLOCK,
  input  Register_Clear,
  output [11:0] DATA_1_RS,
  output [11:0] DATA_2_RT
);

  wire and_1_out, and_2_out, and_3_out, and_4_out, and_5_out, and_6_out, and_7_out, and_8_out,
       decoder_1_out0, decoder_1_out1, decoder_1_out2, decoder_1_out3, decoder_1_out4, decoder_1_out5,
       decoder_1_out6, decoder_1_out7;
  wire [11:0] R0_q, R1_q, R2_q, R3_q, R4_q, R5_q, R6_q, R7_q;

  Decoder #(.select(3), .enable("false")) decoder_1 (
    .out0(decoder_1_out0), .out1(decoder_1_out1), .out2(decoder_1_out2), .out3(decoder_1_out3),
    .out4(decoder_1_out4), .out5(decoder_1_out5), .out6(decoder_1_out6), .out7(decoder_1_out7),
    .sel(RD_Selector));
  and and_1 (and_1_out, Write_Enabler, decoder_1_out0);
  and and_2 (and_2_out, Write_Enabler, decoder_1_out1);
  and and_3 (and_3_out, Write_Enabler, decoder_1_out2);
  and and_4 (and_4_out, Write_Enabler, decoder_1_out3);
  Register #(.width(12)) R0 (.D(Write_Data), .en(and_1_out), .Q(R0_q), .clk(CLOCK), .clr(Register_Clear));
  Register #(.width(12)) R1 (.D(Write_Data), .en(and_2_out), .Q(R1_q), .clk(CLOCK), .clr(Register_Clear));
  Register #(.width(12)) R2 (.D(Write_Data), .en(and_3_out), .Q(R2_q), .clk(CLOCK), .clr(Register_Clear));
  Register #(.width(12)) R3 (.D(Write_Data), .en(and_4_out), .Q(R3_q), .clk(CLOCK), .clr(Register_Clear));
  Register #(.width(12)) R7 (.D(Write_Data), .en(and_5_out), .Q(R7_q), .clk(CLOCK), .clr(Register_Clear));
  Register #(.width(12)) R6 (.D(Write_Data), .en(and_6_out), .Q(R6_q), .clk(CLOCK), .clr(Register_Clear));
  Register #(.width(12)) R5 (.D(Write_Data), .en(and_7_out), .Q(R5_q), .clk(CLOCK), .clr(Register_Clear));
  Register #(.width(12)) R4 (.D(Write_Data), .en(and_8_out), .Q(R4_q), .clk(CLOCK), .clr(Register_Clear));
  and and_5 (and_5_out, Write_Enabler, decoder_1_out7);
  and and_6 (and_6_out, Write_Enabler, decoder_1_out6);
  and and_7 (and_7_out, Write_Enabler, decoder_1_out5);
  and and_8 (and_8_out, Write_Enabler, decoder_1_out4);
  Multiplexer #(.select(3), .width(12), .enable("false")) multiplexer_1 (
    .in0(R0_q), .in1(R1_q), .in2(R2_q), .in3(R3_q), .in4(R4_q), .in5(R5_q), .in6(R6_q), .in7(R7_q),
    .out(DATA_1_RS), .sel(RS_Selector));
  Multiplexer #(.select(3), .width(12), .enable("false")) multiplexer_2 (
    .in0(R0_q), .in1(R1_q), .in2(R2_q), .in3(R3_q), .in4(R4_q), .in5(R5_q), .in6(R6_q), .in7(R7_q),
    .out(DATA_2_RT), .sel(RT_Selector));
endmodule

module ALU_12_bit (
  input  [11:0] A,
  input  [11:0] B,
  input  [2:0] ALUOP,
  output Zero_Detector,
  output [11:0] Result,
  output [11:0] Cout___Bout___Upper_Bits_of_Product___Remainder
);

  wire adder_1_cout, subtractor_1_bout;
  wire [11:0] adder_1_out, and_1_out, bit_extender_1_out, bit_extender_2_out, divider_1_out, divider_1_rem,
       multiplier_1_cout, multiplier_1_out, not_1_out, or_1_out, subtractor_1_out, xor_1_out;

  assign not_1_out = ~A;  // NOT_Gate not_1, 12 bits wide
  Adder #(.width(12)) adder_1 (.a(A), .b(B), .out(adder_1_out), .cout(adder_1_cout));  // open: cin
  Subtractor #(.width(12)) subtractor_1 (.a(A), .b(B), .out(subtractor_1_out), .bout(subtractor_1_bout));  // open: bin
  Multiplier #(.width(12)) multiplier_1 (.a(A), .b(B), .out(multiplier_1_out), .cout(multiplier_1_cout));  // open: cin
  Divider #(.width(12)) divider_1 (.a(A), .b(B), .out(divider_1_out), .rem(divider_1_rem));  // open: upper
  assign and_1_out = A & B;  // AND_Gate and_1, 12 bits wide
  assign or_1_out = A | B;  // OR_Gate or_1, 12 bits wide
  assign xor_1_out = A ^ B;  // XOR_Gate xor_1, 12 bits wide
  Multiplexer #(.select(3), .width(12), .enable("false")) multiplexer_1 (
    .in0(and_1_out), .in1(or_1_out), .in2(not_1_out), .in3(xor_1_out), .in4(adder_1_out),
    .in5(subtractor_1_out), .in6(multiplier_1_out), .in7(divider_1_out), .out(Result), .sel(ALUOP));
  assign bit_extender_1_out = {{11{1'b0}}, adder_1_cout};  // Bit_Extender bit_extender_1
  assign bit_extender_2_out = {{11{1'b0}}, subtractor_1_bout};  // Bit_Extender bit_extender_2
  Multiplexer #(.select(3), .width(12), .enable("false")) multiplexer_2 (
    .in0({12{1'b0}}), .in1({12{1'b0}}), .in2({12{1'b0}}), .in3({12{1'b0}}), .in4(bit_extender_1_out),
    .in5(bit_extender_2_out), .in6(multiplier_1_cout), .in7(divider_1_rem),
    .out(Cout___Bout___Upper_Bits_of_Product___Remainder), .sel(ALUOP));
  nor nor_1 (Zero_Detector, Result[0], Result[1], Result[2], Result[3], Result[4], Result[5], Result[6], Result[7], Result[8], Result[9], Result[10], Result[11]);
endmodule

module datapath (
  output [11:0] Jump_Address,
  output [8:0] Jump_Target,
  output [2:0] Opcode,
  output [11:0] Next_Instruction,
  output [2:0] RS_Read_Reg_1,
  output [11:0] Data_01,
  output [11:0] Data_02,
  output [2:0] RT_Read_Reg_2,
  output Zero_Detector,
  output [11:0] Result_Val,
  output [2:0] Write_Register,
  output [11:0] Cout___Bout__Remainder,
  output [11:0] Data_for_Store
);

  wire and_1_out, CLK_out, CLR_2_out, CLR_3_out, CLR_out, control_unit_1_alu_src, control_unit_1_beq_control,
       control_unit_1_jump, control_unit_1_load_enb, control_unit_1_ram_to_reg, control_unit_1_reg_dst,
       control_unit_1_store_enb, control_unit_1_write_enb;
  wire [2:0] control_unit_1_alu_op, multiplexer_2_out;
  wire [11:0] adder_2_out, alu_12_bit_1_result, bit_extender_1_out, multiplexer_1_out, multiplexer_3_out,
       PC_q, ram_1_data;

  control_unit control_unit_1 (
    .opcode(Opcode), .Reg_Dst(control_unit_1_reg_dst), .Write_Enb(control_unit_1_write_enb),
    .ALU_OP(control_unit_1_alu_op), .ALU_Src(control_unit_1_alu_src), .Store_Enb(control_unit_1_store_enb),
    .Load_Enb(control_unit_1_load_enb), .RAM_to_Reg(control_unit_1_ram_to_reg),
    .BEQ_Control(control_unit_1_beq_control), .Jump(control_unit_1_jump));
  Multiplexer #(.width(12), .enable("false")) multiplexer_1 (
    .in0(multiplexer_3_out), .in1(Jump_Address), .out(multiplexer_1_out), .sel(control_unit_1_jump));
  Register #(.width(12)) PC (.D(multiplexer_1_out), .Q(PC_q), .clk(CLK_out), .clr(CLR_out));  // open: en
  Button CLR (.out(CLR_out));
  Clock CLK (.out(CLK_out));
  Adder #(.width(12)) adder_1 (
    .a(PC_q), .b(12'h1), .out({Jump_Address[11:9], Next_Instruction[8:0]}));  // open: cin, cout
  ROM #(.addrWidth(12), .dataWidth(12)) rom_1 (.addr(PC_q), .data({Opcode, Jump_Address[8:0]}));  // open: sel
  Adder #(.width(12)) adder_2 (
    .a({Jump_Address[11:9], Next_Instruction[8:0]}), .b(bit_extender_1_out), .out(adder_2_out));  // open: cin, cout
  Multiplexer #(.width(3), .enable("false")) multiplexer_2 (
    .in0(Jump_Address[2:0]), .in1(Jump_Address[5:3]), .out(multiplexer_2_out), .sel(control_unit_1_reg_dst));
  Multiplexer #(.width(12), .enable("false")) multiplexer_3 (
    .in0({Jump_Address[11:9], Next_Instruction[8:0]}), .in1(adder_2_out), .out(multiplexer_3_out),
    .sel(and_1_out));
  register_file_12_bit register_file_12_bit_1 (
    .Write_Enabler(control_unit_1_write_enb), .Write_Data(Result_Val), .RD_Selector(multiplexer_2_out),
    .DATA_1_RS(Data_01), .RS_Selector(Jump_Address[8:6]), .DATA_2_RT(Data_for_Store),
    .RT_Selector(Jump_Address[5:3]), .CLOCK(CLK_out), .Register_Clear(CLR_2_out));
  Button CLR_2 (.out(CLR_2_out));
  assign bit_extender_1_out = {{9{1'b0}}, Jump_Address[2:0]};  // Bit_Extender bit_extender_1
  and and_1 (and_1_out, Zero_Detector, control_unit_1_beq_control);
  Multiplexer #(.width(12), .enable("false")) multiplexer_4 (
    .in0(Data_for_Store), .in1(bit_extender_1_out), .out(Data_02), .sel(control_unit_1_alu_src));
  ALU_12_bit alu_12_bit_1 (
    .A(Data_01), .B(Data_02), .Zero_Detector(Zero_Detector), .Result(alu_12_bit_1_result),
    .ALUOP(control_unit_1_alu_op), .Cout___Bout___Upper_Bits_of_Product___Remainder(Cout___Bout__Remainder));
  RAM #(.addrWidth(12), .dataWidth(12), .bus("separate")) ram_1 (
    .addr(alu_12_bit_1_result), .din(Data_for_Store), .data(ram_1_data), .str(control_unit_1_store_enb),
    .clk(CLK_out), .ld(control_unit_1_load_enb), .clr(CLR_3_out));  // open: sel
  Button CLR_3 (.out(CLR_3_out));
  Multiplexer #(.width(12), .enable("false")) multiplexer_5 (
    .in0(alu_12_bit_1_result), .in1(ram_1_data), .out(Result_Val), .sel(control_unit_1_ram_to_reg));

  assign Jump_Target = Jump_Address[8:0];
  assign Next_Instruction[11:9] = Jump_Address[11:9];
  assign RS_Read_Reg_1 = Jump_Address[8:6];
  assign RT_Read_Reg_2 = Jump_Address[5:3];
  assign Write_Register = Jump_Address[2:0];

  // Notes on the sheet:
  //   contents of rom_1 (hex, n*v repeats v):
  //   53 32e 5ca 6e5 9f2 a8c ce5 e0a
endmodule

module control_unit (
  input  [2:0] opcode,
  output Reg_Dst,
  output Write_Enb,
  output [2:0] ALU_OP,
  output ALU_Src,
  output Store_Enb,
  output Load_Enb,
  output RAM_to_Reg,
  output BEQ_Control,
  output Jump
);

  wire and_2_out, and_3_out, and_4_out, and_6_out, and_7_out, and_8_out, and_9_out, not_1_out, not_2_out,
       not_3_out, not_4_out, not_5_out, not_6_out, not_7_out, not_8_out, not_9_out, not_10_out, not_11_out,
       not_12_out, not_13_out, not_14_out, not_15_out, not_16_out, not_17_out, not_18_out, not_19_out;

  not not_1 (not_1_out, opcode[2]);
  not not_2 (not_2_out, opcode[1]);
  not not_3 (not_3_out, opcode[1]);
  not not_4 (not_4_out, opcode[0]);
  not not_5 (not_5_out, opcode[2]);
  not not_6 (not_6_out, opcode[1]);
  not not_7 (not_7_out, opcode[0]);
  not not_8 (not_8_out, opcode[2]);
  not not_9 (not_9_out, opcode[2]);
  not not_10 (not_10_out, opcode[0]);
  not not_11 (not_11_out, opcode[2]);
  not not_12 (not_12_out, opcode[1]);
  not not_13 (not_13_out, opcode[1]);
  not not_14 (not_14_out, opcode[1]);
  not not_15 (not_15_out, opcode[0]);
  not not_16 (not_16_out, opcode[1]);
  not not_17 (not_17_out, opcode[0]);
  not not_18 (not_18_out, opcode[0]);
  and and_1 (Jump, opcode[2], opcode[1], opcode[0]);
  and and_2 (and_2_out, not_1_out, opcode[1]);
  and and_3 (and_3_out, opcode[2], not_2_out);
  not not_19 (not_19_out, opcode[2]);
  and and_4 (and_4_out, not_3_out, not_4_out);
  or or_1 (ALU_OP[2], not_5_out, not_6_out, not_7_out);
  and and_5 (ALU_OP[1], not_8_out, opcode[1]);
  and and_6 (and_6_out, not_9_out, opcode[0]);
  and and_7 (and_7_out, opcode[2], opcode[1], not_10_out);
  and and_8 (and_8_out, not_11_out, opcode[1]);
  and and_9 (and_9_out, opcode[2], not_12_out);
  and and_10 (Store_Enb, opcode[2], not_13_out, opcode[0]);
  and and_11 (Load_Enb, opcode[2], not_14_out, not_15_out);
  and and_12 (RAM_to_Reg, opcode[2], not_16_out, not_17_out);
  and and_13 (BEQ_Control, opcode[2], opcode[1], not_18_out);
  or or_2 (Reg_Dst, and_2_out, and_3_out);
  or or_3 (Write_Enb, not_19_out, and_4_out);
  or or_4 (ALU_OP[0], and_6_out, and_7_out);
  or or_5 (ALU_Src, and_8_out, and_9_out);
endmodule
