// Logisim project ALU 12-bit.circ as structural Verilog: 2 circuits, main circuit main
module main (
);

  ALU_12_bit alu_12_bit_1 ();  // open: A, B, Zero_Detector, Result, ALUOP, Cout___Bout___Upper_Bits_of_Product___Remainder
endmodule

module ALU_12_bit (
  input  [11:0] A,
  input  [11:0] B,
  input  [2:0] ALUOP,
  output Zero_Detector,
  output [11:0] Result,
  output [11:0] Cout___Bout___Upper_Bits_of_Product___Remainder
);

  wire adder_1_cout, subtractor_1_bout;
  wire [11:0] adder_1_out, and_1_out, bit_extender_1_out, bit_extender_2_out, divider_1_out, divider_1_rem,
       multiplier_1_cout, multiplier_1_out, not_1_out, or_1_out, subtractor_1_out, xor_1_out;

  assign not_1_out = ~A;  // NOT_Gate not_1, 12 bits wide
  Adder #(.width(12)) adder_1 (.a(A), .b(B), .out(adder_1_out), .cout(adder_1_cout));  // open: cin
  Subtractor #(.width(12)) subtractor_1 (.a(A), .b(B), .out(subtractor_1_out), .bout(subtractor_1_bout));  // open: bin
  Multiplier #(.width(12)) multiplier_1 (.a(A), .b(B), .out(multiplier_1_out), .cout(multiplier_1_cout));  // open: cin
  Divider #(.width(12)) divider_1 (.a(A), .b(B), .out(divider_1_out), .rem(divider_1_rem));  // open: upper
  assign and_1_out = A & B;  // AND_Gate and_1, 12 bits wide
  assign or_1_out = A | B;  // OR_Gate or_1, 12 bits wide
  assign xor_1_out = A ^ B;  // XOR_Gate xor_1, 12 bits wide
  Multiplexer #(.select(3), .width(12), .enable("false")) multiplexer_1 (
    .in0(and_1_out), .in1(or_1_out), .in2(not_1_out), .in3(xor_1_out), .in4(adder_1_out),
    .in5(subtractor_1_out), .in6(multiplier_1_out), .in7(divider_1_out), .out(Result), .sel(ALUOP));
  assign bit_extender_1_out = {{11{1'b0}}, adder_1_cout};  // Bit_Extender bit_extender_1
  assign bit_extender_2_out = {{11{1'b0}}, subtractor_1_bout};  // Bit_Extender bit_extender_2
  Multiplexer #(.select(3), .width(12), .enable("false")) multiplexer_2 (
    .in0({12{1'b0}}), .in1({12{1'b0}}), .in2({12{1'b0}}), .in3({12{1'b0}}), .in4(bit_extender_1_out),
    .in5(bit_extender_2_out), .in6(multiplier_1_cout), .in7(divider_1_rem),
    .out(Cout___Bout___Upper_Bits_of_Product___Remainder), .sel(ALUOP));
  nor nor_1 (Zero_Detector, Result[0], Result[1], Result[2], Result[3], Result[4], Result[5], Result[6], Result[7], Result[8], Result[9], Result[10], Result[11]);
endmodule
